# Fritzing sketch Nano_Nrf95w_CO_AM312_V1 (saved by Fritzing 0.9.3b)
circuit board: 6.8cm x 3.6cm
breadboards: 1

parts:
  RFM95W = RFM9xW
  74HC4050 = 74HC4050 [package=so16]
  Arduino_Nano = Arduino Nano (Rev3.0)
  HiLink = HLK-2M05
  230V_area = female pin header, 1 pin [form="♀ (female)"]
  230V_area1 = female pin header, 1 pin [form="♀ (female)"]
  MQ = female pin header, 4 pins [form="♀ (female)"]
  C1 = Electrolytic Capacitor [capacitance=1µF package="100 mil [THT, electrolytic]"]
  AM312 = female pin header, 3 pins [form="♀ (female)"]

nets:
  GND: RFM95W.GND, 74HC4050.GND, Arduino_Nano.GND, HiLink.-Vo, MQ.pin2, C1.-, AM312.pin3
  N1: RFM95W.MISO, Arduino_Nano.D12/MISO
  N2: RFM95W.MOSI, 74HC4050.5Y
  N3: RFM95W.SCK, 74HC4050.2Y
  N4: RFM95W.NSS, 74HC4050.6Y
  N5: RFM95W.RESET, Arduino_Nano.RESET
  VCC: RFM95W.VCC, 74HC4050.VCC, Arduino_Nano.3V3
  N6: RFM95W.DIO0, Arduino_Nano.D7
  N7: RFM95W.DIO1, Arduino_Nano.D8
  N8: RFM95W.DIO2, Arduino_Nano.D9
  N9: 74HC4050.2A, Arduino_Nano.D13/SCK
  N10: 74HC4050.5A, Arduino_Nano.D11/MOSI
  N11: 74HC4050.6A, Arduino_Nano.D10
  N12: Arduino_Nano.D2, AM312.pin2
  N13: Arduino_Nano.5V, HiLink.+Vo, MQ.pin1, C1.+, AM312.pin1
  N14: Arduino_Nano.A0, MQ.pin4
  N15: HiLink.AC#0, 230V_area1.pin1
  N16: HiLink.AC#1, 230V_area.pin1

custom parts:
  RFM9xW: RFM9xW Module connector
  74HC4050: Hex non-inverting HIGH-to-LOW level shifter
  HLK-2M05: AC-DC 220V to 5V Step-Down Power Supply Module (2Watt)
